# Fritzing sketch HX711_5Kg (saved by Fritzing 0.9.3b)

parts:
  元件1 = Arduino Uno (Rev3)
  元件2 = HX711 Weighing Sensor Module

nets:
  GND: 元件1.GND, 元件2.GND
  N1: 元件1.D2, 元件2.CK/TX
  N2: 元件1.D3_PWM, 元件2.DO/RX
  5V: 元件1.5V, 元件2.VCC

notes:
  SegmentLCD
  CS WR DATA GND VCC
  A- H
  A+ X
  E- 711
  E+
