# Fritzing sketch hx711_loadcell (saved by Fritzing 0.9.3b)

parts:
  元件1 = Arduino Uno (Rev3)
  元件2 = HX711 Weighing Sensor Module

nets:
  N1: 元件1.A0, 元件2.DO/RX
  N2: 元件1.A1, 元件2.CK/TX
  5V: 元件1.5V, 元件2.VCC
  GND: 元件1.GND, 元件2.GND

notes:
  E+ E- S+ S-
  Load Cell 200kN
