# Fritzing sketch 连接图 (saved by Fritzing 0.8.3b)

parts:
  元件1 = Arduino Uno (Rev3)
  U1 = HX711
  U2 = HX711
  U3 = 实时时钟模块DS1302

nets:
  VCC: 元件1.5V, U1.VCC, U3.VCC
  GND: 元件1.GND, U1.GND, U3.GND
  N1: 元件1.D2, U1.SCK
  N2: 元件1.D3_PWM, U1.DT
  N3: 元件1.D4, U3.DATA
  N4: 元件1.D5_PWM, U3.WR
  N5: 元件1.D6_PWM, U3.CS
  N6: U1.E+, U2.PIN1
  N7: U1.E-, U2.PIN2
  N8: U1.A-, U2.PIN3
  N9: U1.A+, U2.PIN4
